// Digital circuit PC_ROM_SPLITTER_4_REGS.dig as structural Verilog
module PC_ROM_SPLITTER_4_REGS (
  input  clk,
  input  PC_RESET,
  input  C_I,
  input  C_I_2,
  output [3:0] op_code,
  output [3:0] RS,
  output [19:0] result,
  output addr_carry,
  output [3:0] RD,
  output [19:0] DATA,
  output [31:0] CUR_INST_DATA
);

  wire add_1_c_o, op_add, op_addi, op_load, op_mult, op_store, op_sub, op_write, or_1_out, or_2_out,
       sub_1_c_o;
  wire [7:0] PC_out;
  wire [19:0] add_1_s, Da, Db, multiplexer_1_out, registerfile_1_db, sub_1_s;
  wire [39:0] mul_1_mul;
  wire [39:20] driver_1_out;

  Counter #(.Bits(8)) PC (.en(clk), .C(clk), .clr(PC_RESET), .out(PC_out));  // open: ovf
  ROM #(.AddrBits(8), .Bits(32)) INSTR_MEM (.A(PC_out), .sel(1'b1), .D(CUR_INST_DATA));
  Decoder #(.Selector_Bits(4)) decoder_1 (
    .sel(CUR_INST_DATA[31:28]), .out_0(op_write), .out_1(op_add), .out_2(op_addi), .out_3(op_sub),
    .out_4(op_mult), .out_5(op_store), .out_6(op_load));  // open: out_7, out_8, out_9, out_10, out_11, out_12, out_13, out_14, out_15
  or or_1 (or_1_out, op_write, op_load);
  or or_2 (or_2_out, op_add, op_write, op_mult, op_sub, op_addi);
  Add #(.Bits(20)) add_1 (.a(Da), .b(Db), .c_i(C_I), .s(add_1_s), .c_o(add_1_c_o));
  Sub #(.Bits(20)) sub_1 (.a(Da), .b(Db), .c_i(C_I_2), .s(sub_1_s), .c_o(sub_1_c_o));
  Mul #(.Bits(20)) mul_1 (.a(Da), .b(Db), .mul(mul_1_mul));
  Multiplexer #(.Bits(20)) multiplexer_1 (
    .sel(or_1_out), .in_0(result), .in_1(CUR_INST_DATA[19:0]), .out(multiplexer_1_out));
  assign {driver_1_out, result} = op_mult ? mul_1_mul : 40'bz;  // Driver driver_1
  RegisterFile #(.AddrBits(4), .Bits(20)) registerfile_1 (
    .Din(multiplexer_1_out), .we(or_2_out), .Rw(CUR_INST_DATA[27:24]), .C(clk), .Ra(CUR_INST_DATA[27:24]),
    .Rb(CUR_INST_DATA[23:20]), .Da(Da), .Db(registerfile_1_db));
  assign result = op_add ? add_1_s : 20'bz;  // Driver driver_2
  assign addr_carry = op_add ? add_1_c_o : 1'bz;  // Driver driver_3
  assign result = op_sub ? sub_1_s : 20'bz;  // Driver driver_4
  assign addr_carry = op_sub ? sub_1_c_o : 1'bz;  // Driver driver_5
  RAMDualPort #(.AddrBits(4), .Bits(20)) ramdualport_1 (
    .A(CUR_INST_DATA[27:24]), .Din(Db), .str(op_store), .C(clk), .ld(op_load), .D(result));
  Multiplexer #(.Bits(20)) multiplexer_2 (
    .sel(op_addi), .in_0(registerfile_1_db), .in_1(CUR_INST_DATA[19:0]), .out(Db));

  assign DATA = CUR_INST_DATA[19:0];
  assign op_code = CUR_INST_DATA[31:28];
  assign RD = CUR_INST_DATA[27:24];
  assign RS = CUR_INST_DATA[23:20];

  // Other names for the same wires on the sheet: C = clk; CARRY = addr_carry; inst_bin[31:0] = CUR_INST_DATA;
  //   OP[3:0] = CUR_INST_DATA[31:28]; reset = PC_RESET

  // Notes on the sheet:
  //   contents of INSTR_MEM (hex, n*v repeats v):
  //   100000a,2000014,11200000,52100000,62000000,4000064,53400000,63000000
endmodule
